# Fritzing sketch PiLone rev D 3v low spec (saved by Fritzing 0.8.7b)
circuit board: 2.43976cm x 4.03975cm
breadboards: 1

parts:
  J1 = male pin header, 4 pins [form="♂ (male)"]
  J3 = male pin header, 4 pins [form="♂ (male)"]
  J2 = male pin header, 4 pins [form="♂ (male)"]
  PWR_IN = mystery part, 2 pins [chip_label="PWR IN 5V"]
  PWR_OUT = mystery part, 2 pins [chip_label="PWR OUT 5V"]
  Raspberry_Pi_B_rev1 = Raspberry Pi B rev2
  ProMini_3V_8MHz = Arduino Pro Mini v13

nets:
  GND: J1.pin1, J1.pin4, J3.pin1, J3.pin4, J2.pin1, J2.pin4, PWR_IN.pin2, PWR_OUT.pin2, Raspberry_Pi_B_rev1.GND, ProMini_3V_8MHz.GND
  N1: J1.pin2, ProMini_3V_8MHz.D2
  N2: J1.pin3, J3.pin3, J2.pin3, PWR_IN.pin1, PWR_OUT.pin1, ProMini_3V_8MHz.RAW
  N3: J3.pin2, ProMini_3V_8MHz.D4
  N4: J2.pin2, ProMini_3V_8MHz.D3_PWM
  N5: Raspberry_Pi_B_rev1.GPIO_14, ProMini_3V_8MHz.D1/RX
  N6: Raspberry_Pi_B_rev1.GPIO_15, ProMini_3V_8MHz.D0/TX

notes:
  <->
  solder USB micro cable here
  Power In
  PiLone
  Rev D 3V
